// Logisim project hw3.circ as structural Verilog: 10 circuits, main circuit 1-bit adder
module Main (
  input  [4:0] ALUOp,
  input  [2:0] RegA,
  input  [2:0] RegB,
  input  WWrite,
  input  [2:0] RegW,
  input  [15:0] WIn,
  input  CondUpdate,
  input  Reset,
  output Z,
  output C,
  output N,
  output V,
  output [15:0] ALUOut
);

  wire Clock_out;
  wire [3:0] n16_bit_alu_1_condcodes;
  wire [15:0] register_file_1_a_bus, register_file_1_b_bus, WOut;

  Clock Clock (.out(Clock_out));
  Register_File register_file_1 (
    .Clk(Clock_out), .WEn(WWrite), ._0(Reset), .ASel(RegA), .A_Bus(register_file_1_a_bus), .BSel(RegB),
    .B_Bus(register_file_1_b_bus), .W_Bus(WOut), .WData(WIn), .WSel(RegW));
  _16_bit_ALU u_16_bit_alu_1 (
    .Result(ALUOut), .A(register_file_1_a_bus), .B(register_file_1_b_bus), .Operations(ALUOp),
    .CondCodes(n16_bit_alu_1_condcodes));
  Register #(.width(4)) CondCodes (
    .D(n16_bit_alu_1_condcodes), .en(CondUpdate), .Q({V, N, C, Z}), .clk(Clock_out), .clr(Reset));

  // Other names for the same wires on the sheet: CondCodes[3:0] = {V, N, C, Z}

  // Notes on the sheet:
  //   Casey Grove - hw3
endmodule

module _16_bit_ALU (
  input  [4:0] Operations,
  input  [15:0] A,
  input  [15:0] B,
  output [3:0] CondCodes,
  output [15:0] Result
);

  wire and_2_out, and_3_out, and_4_out, and_5_out;
  wire [15:0] add_result, and_result, or_result, sub_result;

  add add (.A(A), .B(B), .Result(add_result), .Overflow(CondCodes[1]));
  sub sub (.A(A), .B(B), .Result(sub_result));
  \and  \and  (.A(A), .B(B), .Result(and_result));
  \or  \or  (.A(A), .B(B), .Result(or_result));
  Multiplexer #(.select(5), .width(16), .enable("false")) multiplexer_1 (
    .in0(or_result), .in1(add_result), .in2(and_result), .in3(add_result), .in5(sub_result),
    .in7(add_result), .in9(add_result), .in11(add_result), .in15(add_result), .in16(or_result),
    .in17(add_result), .in18(and_result), .in21(sub_result), .in23(add_result),
    .out({CondCodes[2], Result[14:0]}), .sel(Operations));  // open: in4, in6, in8, in10, in12, in13, in14, in19, in20, in22, in24, in25, in26, in27, in28, in29, in30, in31
  and and_2 (and_2_out, B[15], A[15]);
  and and_3 (and_3_out, ~B[15], ~A[15]);  // AND_Gate
  nor nor_1 (CondCodes[0], CondCodes[2], Result[14], Result[13], Result[12], Result[11], Result[10], Result[9], Result[8], Result[7], Result[6], Result[5], Result[4], Result[3], Result[2], Result[1], Result[0]);
  or or_2 (CondCodes[3], and_4_out, and_5_out);
  and and_4 (and_4_out, ~CondCodes[2], and_2_out);  // AND_Gate
  and and_5 (and_5_out, and_3_out, CondCodes[2]);

  assign Result[15] = CondCodes[2];

  // Other names for the same wires on the sheet: carry = CondCodes[1]; overflow = CondCodes[3]
endmodule

module Register_File (
  input  [15:0] WData,
  input  [2:0] ASel,
  input  Clk,
  input  [2:0] BSel,
  input  WEn,
  input  _0,
  input  [2:0] WSel,
  output [15:0] A_Bus,
  output [15:0] B_Bus,
  output [15:0] W_Bus
);

  wire and_1_out, decoder_1_out0, decoder_1_out1, decoder_1_out2, decoder_1_out3, decoder_1_out4,
       decoder_1_out5, decoder_1_out6, decoder_1_out7;
  wire [15:0] R0_q, R1_q, R2_q, R3_q, R4_q, R5_q, R6_q, R7_q;

  and and_1 (and_1_out, WEn, ~Clk);  // AND_Gate
  Decoder #(.select(3), .disabled(0)) decoder_1 (
    .out0(decoder_1_out0), .out1(decoder_1_out1), .out2(decoder_1_out2), .out3(decoder_1_out3),
    .out4(decoder_1_out4), .out5(decoder_1_out5), .out6(decoder_1_out6), .out7(decoder_1_out7), .sel(WSel),
    .en(and_1_out));
  Register #(.width(16)) R0 (.D(WData), .en(decoder_1_out0), .Q(R0_q), .clk(Clk), .clr(_0));
  Register #(.width(16)) R4 (.D(WData), .en(decoder_1_out4), .Q(R4_q), .clk(Clk), .clr(_0));
  Register #(.width(16)) R1 (.D(WData), .en(decoder_1_out1), .Q(R1_q), .clk(Clk), .clr(_0));
  Register #(.width(16)) R5 (.D(WData), .en(decoder_1_out5), .Q(R5_q), .clk(Clk), .clr(_0));
  Register #(.width(16)) R2 (.D(WData), .en(decoder_1_out2), .Q(R2_q), .clk(Clk), .clr(_0));
  Register #(.width(16)) R3 (.D(WData), .en(decoder_1_out3), .Q(R3_q), .clk(Clk), .clr(_0));
  Register #(.width(16)) R6 (.D(WData), .en(decoder_1_out6), .Q(R6_q), .clk(Clk), .clr(_0));
  Register #(.width(16)) R7 (.D(WData), .en(decoder_1_out7), .Q(R7_q), .clk(Clk), .clr(_0));
  Multiplexer #(.select(3), .width(16), .enable("false")) multiplexer_1 (
    .in0(R0_q), .in1(R1_q), .in2(R2_q), .in3(R3_q), .in4(R4_q), .in5(R5_q), .in6(R6_q), .in7(R7_q),
    .out(A_Bus), .sel(ASel));
  Multiplexer #(.select(3), .width(16), .enable("false")) multiplexer_2 (
    .in0(R0_q), .in1(R1_q), .in2(R2_q), .in3(R3_q), .in4(R4_q), .in5(R5_q), .in6(R6_q), .in7(R7_q),
    .out(B_Bus), .sel(BSel));
  Multiplexer #(.select(3), .width(16), .enable("false")) multiplexer_3 (
    .in0(R0_q), .in1(R1_q), .in2(R2_q), .in3(R3_q), .in4(R4_q), .in5(R5_q), .in6(R6_q), .in7(R7_q),
    .out(W_Bus), .sel(WSel));
endmodule

module _1_bit_adder (
  input  CarryIn,
  input  A,
  input  B,
  output CarryOut,
  output Sum
);

  wire and_1_out, and_2_out, and_3_out, xor_1_out;

  and and_1 (and_1_out, A, CarryIn);
  and and_2 (and_2_out, B, CarryIn);
  and and_3 (and_3_out, A, B);
  xor xor_1 (xor_1_out, A, B);
  or or_1 (CarryOut, and_1_out, and_2_out, and_3_out);
  xor xor_2 (Sum, xor_1_out, CarryIn);
endmodule

module _4_bit_adder (
  input  carryIn,
  input  [3:0] A,
  input  [3:0] B,
  output [3:0] Sum,
  output carryOut
);

  wire n1_bit_adder_1_carryout, n1_bit_adder_2_carryout, n1_bit_adder_3_carryout;

  _1_bit_adder u_1_bit_adder_1 (
    .A(A[0]), .B(B[0]), .Sum(Sum[0]), .CarryIn(carryIn), .CarryOut(n1_bit_adder_1_carryout));
  _1_bit_adder u_1_bit_adder_2 (
    .A(A[1]), .B(B[1]), .Sum(Sum[1]), .CarryIn(n1_bit_adder_1_carryout), .CarryOut(n1_bit_adder_2_carryout));
  _1_bit_adder u_1_bit_adder_3 (
    .A(A[2]), .B(B[2]), .Sum(Sum[2]), .CarryIn(n1_bit_adder_2_carryout), .CarryOut(n1_bit_adder_3_carryout));
  _1_bit_adder u_1_bit_adder_4 (
    .A(A[3]), .B(B[3]), .Sum(Sum[3]), .CarryIn(n1_bit_adder_3_carryout), .CarryOut(carryOut));
endmodule

module _4_bit_counter (
  input  Increment,
  input  Clock,
  input  Reset,
  output [3:0] Output
);

  wire [3:0] adder_sum, bit_extender_1_out;

  assign bit_extender_1_out = {{3{1'b0}}, Increment};  // Bit_Extender bit_extender_1
  _4_bit_adder adder (.A(Output), .B(bit_extender_1_out), .Sum(adder_sum), .carryIn(1'b0));  // open: carryOut
  Register #(.width(4)) register_1 (.D(adder_sum), .Q(Output), .clk(Clock), .clr(Reset));  // open: en
endmodule

module add (
  input  [15:0] A,
  input  [15:0] B,
  output [15:0] Result,
  output Overflow
);

  wire n4_bit_adder_1_carryout, n4_bit_adder_2_carryout, n4_bit_adder_3_carryout;

  _4_bit_adder u_4_bit_adder_1 (
    .A(A[3:0]), .B(B[3:0]), .Sum(Result[3:0]), .carryOut(n4_bit_adder_1_carryout), .carryIn(Overflow));
  _4_bit_adder u_4_bit_adder_2 (
    .A(A[7:4]), .B(B[7:4]), .Sum(Result[7:4]), .carryOut(n4_bit_adder_2_carryout),
    .carryIn(n4_bit_adder_1_carryout));
  _4_bit_adder u_4_bit_adder_3 (
    .A(A[11:8]), .B(B[11:8]), .Sum(Result[11:8]), .carryOut(n4_bit_adder_3_carryout),
    .carryIn(n4_bit_adder_2_carryout));
  _4_bit_adder u_4_bit_adder_4 (
    .A(A[15:12]), .B(B[15:12]), .Sum(Result[15:12]), .carryOut(Overflow), .carryIn(n4_bit_adder_3_carryout));
endmodule

module sub (
  input  [15:0] A,
  input  [15:0] B,
  output [15:0] Result
);

  wire n4_bit_adder_1_carryout, n4_bit_adder_2_carryout, n4_bit_adder_3_carryout, or_1_out, overflow;
  wire [15:0] not_1_out;

  assign not_1_out = ~B;  // NOT_Gate not_1, 16 bits wide
  or or_1 (or_1_out, overflow, 1'b1);
  _4_bit_adder u_4_bit_adder_1 (
    .A(A[3:0]), .B(not_1_out[3:0]), .Sum(Result[3:0]), .carryOut(n4_bit_adder_1_carryout), .carryIn(or_1_out));
  _4_bit_adder u_4_bit_adder_2 (
    .A(A[7:4]), .B(not_1_out[7:4]), .Sum(Result[7:4]), .carryOut(n4_bit_adder_2_carryout),
    .carryIn(n4_bit_adder_1_carryout));
  _4_bit_adder u_4_bit_adder_3 (
    .A(A[11:8]), .B(not_1_out[11:8]), .Sum(Result[11:8]), .carryOut(n4_bit_adder_3_carryout),
    .carryIn(n4_bit_adder_2_carryout));
  _4_bit_adder u_4_bit_adder_4 (
    .A(A[15:12]), .B(not_1_out[15:12]), .Sum(Result[15:12]), .carryOut(overflow),
    .carryIn(n4_bit_adder_3_carryout));
endmodule

module \and  (
  input  [15:0] A,
  input  [15:0] B,
  output [15:0] Result
);

  assign Result = A & B;  // AND_Gate and_1, 16 bits wide
endmodule

module \or  (
  input  [15:0] A,
  input  [15:0] B,
  output [15:0] Result
);

  assign Result = A | B;  // OR_Gate or_1, 16 bits wide
endmodule
